# Fritzing sketch etsen_glas_hightech (saved by Fritzing 0.9.3b)

parts:
  Onderdeel1 = Arduino Nano (Rev3.0)
  LDR = Photocell (LDR) [package=THT]
  DHT22 = Humidity and Temperature Sensor RHT03
  R2 = Resistor [tolerance=±5% resistance=15k package=THT]
  NeoPixel = prefix0000

nets:
  N1: Onderdeel1.GND, LDR.pin_0, DHT22.GND_2, NeoPixel.connector3
  N2: Onderdeel1.D2, NeoPixel.connector2
  N3: Onderdeel1.D8, DHT22.Data-signal
  5V: Onderdeel1.5V, DHT22.Vcc, R2.Pin_1, NeoPixel.connector1
  N4: Onderdeel1.A0, LDR.pin_1, R2.Pin_0
